// Logisim project t4sistemas.circ as structural Verilog: 1 circuit, main circuit main
module main (
  input  \Início ,
  input  Zero,
  input  in_3,
  input  in_4,
  input  in_5,
  input  in_6,
  input  in_7,
  input  in_8
);

  wire clock_1_out, j_k_ff_1_q, j_k_ff_2_q, not_1_out, or_1_out, or_2_out;

  Clock clock_1 (.out(clock_1_out));
  not not_1 (not_1_out, Zero);
  or or_1 (or_1_out, \Início , j_k_ff_1_q);
  or or_2 (or_2_out, j_k_ff_1_q, not_1_out);
  J_K_Flip_Flop j_k_ff_1 (
    .J(j_k_ff_2_q), .clk(clock_1_out), .K(j_k_ff_1_q), .Q(j_k_ff_1_q), .preset(in_3), .en(in_4), .reset(in_5));  // open: Qn
  J_K_Flip_Flop j_k_ff_2 (
    .J(or_1_out), .clk(clock_1_out), .K(or_2_out), .Q(j_k_ff_2_q), .preset(in_6), .en(in_7), .reset(in_8));  // open: Qn
  LED led_1 (.in(j_k_ff_1_q));
  LED led_2 (.in(j_k_ff_2_q));

  // Notes on the sheet:
  //   Clock
  //   JK1
  //   JK0
endmodule
